// Logisim project 2401CS45_Sravan.circ as structural Verilog: 8 circuits, main circuit main
module main (
  input  in_1,
  input  in_2,
  input  in_3
);

  wire clock_1_out, comparator_1_eq, comparator_1_gt, control_1_alu_a, control_1_data, control_1_memread,
       control_1_memwrite, control_1_offfset, control_1_pc, control_1_sp_sel, control_1_writea,
       control_1_writeb, control_1_writesp, control_1_writesp_2, count_1_out_4, not_1_out;
  wire [1:0] control_1_asel, control_1_bsel, control_1_pcsel, new_1_out_5;
  wire [2:0] control_1_alu;
  wire [3:0] bcd_1_out_3, bcd_1_out_4, bcd_1_out_5, bcd_1_out_6, bcd_1_out_7;
  wire [7:0] ram_1_data;
  wire [23:0] alu_1_output, ram_1_data_2;
  wire [31:0] A_q, adder_1_out, B_q, bit_extender_1_out, multiplexer_1_out, multiplexer_2_out,
       multiplexer_3_out, multiplexer_4_out, multiplexer_5_out, multiplexer_6_out, multiplexer_7_out,
       multiplexer_8_out, multiplexer_9_out, multiplexer_10_out, PC_q, ram_2_data, SP_q;
  wire [31:24] alu_1_output_2;

  Multiplexer #(.select(2), .width(32), .enable("false")) multiplexer_1 (
    .in0(adder_1_out), .in1({alu_1_output_2, alu_1_output}), .in2(A_q), .in3(PC_q), .out(multiplexer_1_out),
    .sel(new_1_out_5));
  Multiplexer #(.width(32), .enable("false")) multiplexer_2 (
    .in0({alu_1_output_2, alu_1_output}), .in1(A_q), .out(multiplexer_2_out), .sel(control_1_sp_sel));
  Clock clock_1 (.out(clock_1_out));
  count count_1 (.in_1(clock_1_out), .in_2(new_1_out_5[0]), .in_3(new_1_out_5[1]), .out_4(count_1_out_4));
  Comparator #(.width(32)) comparator_1 (
    .a({32{1'b0}}), .b(A_q), .gt(comparator_1_gt), .eq(comparator_1_eq));  // open: lt
  Register #(.width(32)) PC (.D(multiplexer_1_out), .en(1'b1), .Q(PC_q), .clk(clock_1_out), .clr(in_3));
  Register #(.width(32)) SP (.D(multiplexer_2_out), .en(control_1_writesp_2), .Q(SP_q), .clk(clock_1_out), .clr(in_3));
  bcd bcd_1 (
    .in_1(count_1_out_4), .in_2(in_3), .out_3(bcd_1_out_3), .out_4(bcd_1_out_4), .out_5(bcd_1_out_5),
    .out_6(bcd_1_out_6), .out_7(bcd_1_out_7));
  Adder #(.width(32)) adder_1 (.a(32'h1), .b(PC_q), .out(adder_1_out));  // open: cin, cout
  Hex_Digit_Display hex_digit_display_1 (.value(bcd_1_out_3));  // open: dp
  \new  new_1 (
    .in_1(comparator_1_gt), .in_2(comparator_1_eq), .out_5(new_1_out_5), .in_3(control_1_pcsel),
    .in_4(control_1_pc));
  Hex_Digit_Display hex_digit_display_2 (.value(bcd_1_out_4));  // open: dp
  Hex_Digit_Display hex_digit_display_3 (.value(bcd_1_out_5));  // open: dp
  assign bit_extender_1_out = {{8{ram_1_data_2[23]}}, ram_1_data_2};  // Bit_Extender bit_extender_1
  RAM #(.addrWidth(24), .dataWidth(32)) ram_1 (
    .addr(PC_q[23:0]), .data({ram_1_data_2, ram_1_data}), .sel(1'b1), .clk(clock_1_out), .ld(1'b1), .clr(in_1));
  Hex_Digit_Display hex_digit_display_4 (.value(bcd_1_out_6));  // open: dp
  Hex_Digit_Display hex_digit_display_5 (.value(bcd_1_out_7));  // open: dp
  control control_1 (
    .WriteSP(control_1_writesp), .in_1(ram_1_data), .WriteSP_2(control_1_writesp_2),
    .SP_sel(control_1_sp_sel), .WriteA(control_1_writea), .WriteB(control_1_writeb),
    .MemRead(control_1_memread), .MemWrite(control_1_memwrite), .PC(control_1_pc), .ALU(control_1_alu),
    .ASel(control_1_asel), .BSel(control_1_bsel), .ALU_A(control_1_alu_a), .data(control_1_data),
    .offfset(control_1_offfset), .PCSel(control_1_pcsel));
  Multiplexer #(.select(2), .width(32), .enable("false")) multiplexer_3 (
    .in0({alu_1_output_2, alu_1_output}), .in1(B_q), .in2(ram_2_data), .in3(bit_extender_1_out),
    .out(multiplexer_3_out), .sel(control_1_asel));
  Multiplexer #(.select(2), .width(32), .enable("false")) multiplexer_4 (
    .in0(A_q), .in1({alu_1_output_2, alu_1_output}), .in2(ram_2_data), .in3(bit_extender_1_out),
    .out(multiplexer_4_out), .sel(control_1_bsel));
  Multiplexer #(.width(32), .enable("false")) multiplexer_5 (
    .in0(adder_1_out), .in1(multiplexer_6_out), .out(multiplexer_5_out), .sel(not_1_out));
  Multiplexer #(.width(32), .enable("false")) multiplexer_6 (
    .in0(multiplexer_3_out), .in1(SP_q), .out(multiplexer_6_out), .sel(control_1_writesp));
  not not_1 (not_1_out, control_1_pc);
  Register #(.width(32)) A (.D(multiplexer_5_out), .en(control_1_writea), .Q(A_q), .clk(clock_1_out), .clr(in_3));
  Register #(.width(32)) B (.D(multiplexer_4_out), .en(control_1_writeb), .Q(B_q), .clk(clock_1_out), .clr(in_3));
  Multiplexer #(.width(32), .enable("false")) multiplexer_7 (
    .in0(A_q), .in1(SP_q), .out(multiplexer_7_out), .sel(control_1_alu_a));
  Multiplexer #(.width(32), .enable("false")) multiplexer_8 (
    .in0(multiplexer_7_out), .in1(adder_1_out), .out(multiplexer_8_out), .sel(control_1_pc));
  Multiplexer #(.width(32), .enable("false")) multiplexer_9 (
    .in0(B_q), .in1(bit_extender_1_out), .out(multiplexer_9_out), .sel(control_1_offfset));
  ALU alu_1 (
    .A(multiplexer_8_out), .B(multiplexer_9_out), .\output ({alu_1_output_2, alu_1_output}),
    .in_2(control_1_alu));
  Multiplexer #(.width(32), .enable("false")) multiplexer_10 (
    .in0(A_q), .in1(B_q), .out(multiplexer_10_out), .sel(control_1_data));
  RAM #(.addrWidth(24), .dataWidth(32), .bus("separate")) ram_2 (
    .addr(alu_1_output), .din(multiplexer_10_out), .data(ram_2_data), .str(control_1_memwrite), .sel(1'b1),
    .clk(clock_1_out), .ld(control_1_memread), .clr(in_2));

  // Notes on the sheet:
  //   No of Instructions processed
endmodule

module opcode (
  input  O5,
  input  O4,
  input  O3,
  input  O2,
  input  O1,
  input  O0,
  output WriteA,
  output WriteB,
  output MemRead,
  output MemWrite,
  output PC,
  output ALU2,
  output ALU1,
  output ALU0,
  output A0,
  output A1,
  output B0,
  output OFF
);

  wire and_1_out, and_2_out, and_3_out, and_4_out, and_5_out, and_6_out, and_7_out, and_8_out, and_9_out,
       and_10_out, and_11_out, and_12_out, and_13_out, and_14_out, and_15_out, and_16_out, and_17_out,
       and_18_out, and_19_out, and_20_out, and_21_out, and_22_out, and_23_out, and_24_out, and_25_out,
       and_26_out, and_27_out, and_28_out, and_29_out, and_30_out, and_31_out, and_32_out, and_33_out,
       and_34_out, and_35_out, and_36_out, and_37_out, and_39_out, and_40_out, and_41_out, and_42_out,
       and_43_out, not_1_out, not_2_out, not_3_out, not_4_out, not_5_out, not_6_out, not_7_out, not_8_out,
       not_9_out, not_10_out, not_11_out, not_12_out, not_13_out, not_14_out, not_15_out, not_16_out,
       not_17_out, not_18_out, not_19_out, not_20_out, not_21_out, not_22_out, not_23_out, not_24_out,
       not_25_out, not_26_out, not_27_out, not_28_out, not_29_out, not_30_out, not_31_out, not_32_out,
       not_33_out, not_34_out, not_35_out, not_36_out, not_37_out, not_38_out, not_39_out, not_40_out,
       not_41_out, not_42_out, not_43_out, not_44_out, not_45_out, not_46_out, not_47_out, not_48_out,
       not_49_out, not_50_out, not_51_out, not_52_out, not_53_out, not_54_out, not_55_out, not_56_out,
       not_57_out, not_58_out, not_59_out, not_60_out, not_61_out, not_62_out, not_63_out, not_64_out,
       not_65_out, not_66_out, not_67_out, not_68_out, not_69_out, not_70_out, not_71_out, not_72_out,
       not_73_out, not_74_out, not_75_out, not_76_out, not_77_out, not_78_out, not_79_out, not_80_out,
       not_81_out, not_82_out, not_83_out, not_84_out, not_85_out, not_86_out, not_87_out, not_88_out,
       not_89_out, not_90_out, not_91_out, not_92_out, not_93_out, not_94_out, not_95_out, not_96_out,
       not_97_out, not_98_out, not_99_out, not_100_out, not_101_out, not_102_out, not_103_out, not_104_out,
       not_105_out, not_106_out, not_107_out, not_108_out, not_109_out, not_110_out, not_111_out,
       not_112_out, not_113_out, not_114_out, not_115_out;

  not not_1 (not_1_out, O5);
  not not_2 (not_2_out, O4);
  not not_3 (not_3_out, O3);
  not not_4 (not_4_out, O2);
  not not_5 (not_5_out, O5);
  not not_6 (not_6_out, O4);
  not not_7 (not_7_out, O2);
  not not_8 (not_8_out, O5);
  not not_9 (not_9_out, O4);
  not not_10 (not_10_out, O3);
  not not_11 (not_11_out, O5);
  not not_12 (not_12_out, O4);
  not not_13 (not_13_out, O0);
  not not_14 (not_14_out, O5);
  not not_15 (not_15_out, O4);
  not not_16 (not_16_out, O1);
  not not_17 (not_17_out, O5);
  not not_18 (not_18_out, O4);
  not not_19 (not_19_out, O3);
  not not_20 (not_20_out, O2);
  not not_21 (not_21_out, O0);
  not not_22 (not_22_out, O5);
  not not_23 (not_23_out, O4);
  not not_24 (not_24_out, O1);
  not not_25 (not_25_out, O5);
  not not_26 (not_26_out, O4);
  not not_27 (not_27_out, O3);
  not not_28 (not_28_out, O2);
  not not_29 (not_29_out, O0);
  not not_30 (not_30_out, O5);
  not not_31 (not_31_out, O4);
  not not_32 (not_32_out, O3);
  not not_33 (not_33_out, O1);
  not not_34 (not_34_out, O0);
  not not_35 (not_35_out, O5);
  not not_36 (not_36_out, O4);
  not not_37 (not_37_out, O3);
  not not_38 (not_38_out, O2);
  not not_39 (not_39_out, O5);
  not not_40 (not_40_out, O4);
  not not_41 (not_41_out, O3);
  not not_42 (not_42_out, O1);
  not not_43 (not_43_out, O5);
  not not_44 (not_44_out, O4);
  not not_45 (not_45_out, O5);
  not not_46 (not_46_out, O3);
  not not_47 (not_47_out, O2);
  not not_48 (not_48_out, O1);
  not not_49 (not_49_out, O5);
  not not_50 (not_50_out, O3);
  not not_51 (not_51_out, O2);
  not not_52 (not_52_out, O0);
  not not_53 (not_53_out, O2);
  not not_54 (not_54_out, O0);
  not not_55 (not_55_out, O2);
  not not_56 (not_56_out, O1);
  not not_57 (not_57_out, O3);
  not not_58 (not_58_out, O2);
  not not_59 (not_59_out, O1);
  not not_60 (not_60_out, O5);
  not not_61 (not_61_out, O4);
  not not_62 (not_62_out, O3);
  not not_63 (not_63_out, O2);
  not not_64 (not_64_out, O1);
  not not_65 (not_65_out, O0);
  not not_66 (not_66_out, O5);
  not not_67 (not_67_out, O4);
  not not_68 (not_68_out, O2);
  not not_69 (not_69_out, O5);
  not not_70 (not_70_out, O4);
  not not_71 (not_71_out, O5);
  not not_72 (not_72_out, O4);
  not not_73 (not_73_out, O0);
  not not_74 (not_74_out, O5);
  not not_75 (not_75_out, O3);
  not not_76 (not_76_out, O2);
  not not_77 (not_77_out, O0);
  not not_78 (not_78_out, O5);
  not not_79 (not_79_out, O4);
  not not_80 (not_80_out, O3);
  not not_81 (not_81_out, O2);
  not not_82 (not_82_out, O0);
  not not_83 (not_83_out, O5);
  not not_84 (not_84_out, O4);
  not not_85 (not_85_out, O3);
  not not_86 (not_86_out, O1);
  not not_87 (not_87_out, O0);
  not not_88 (not_88_out, O5);
  not not_89 (not_89_out, O3);
  not not_90 (not_90_out, O2);
  not not_91 (not_91_out, O1);
  not not_92 (not_92_out, O0);
  not not_93 (not_93_out, O5);
  not not_94 (not_94_out, O4);
  not not_95 (not_95_out, O1);
  not not_96 (not_96_out, O5);
  not not_97 (not_97_out, O4);
  not not_98 (not_98_out, O5);
  not not_99 (not_99_out, O4);
  not not_100 (not_100_out, O3);
  not not_101 (not_101_out, O2);
  not not_102 (not_102_out, O5);
  not not_103 (not_103_out, O4);
  not not_104 (not_104_out, O2);
  not not_105 (not_105_out, O0);
  not not_106 (not_106_out, O5);
  not not_107 (not_107_out, O4);
  not not_108 (not_108_out, O3);
  not not_109 (not_109_out, O1);
  not not_110 (not_110_out, O5);
  not not_111 (not_111_out, O4);
  not not_112 (not_112_out, O5);
  not not_113 (not_113_out, O3);
  not not_114 (not_114_out, O2);
  not not_115 (not_115_out, O1);
  and and_1 (and_1_out, not_1_out, not_2_out, not_3_out, not_4_out);
  and and_2 (and_2_out, not_5_out, not_6_out, not_7_out, O0);
  and and_3 (and_3_out, not_8_out, not_9_out, not_10_out, O1);
  and and_4 (and_4_out, not_11_out, not_12_out, O2, not_13_out);
  and and_5 (and_5_out, not_14_out, not_15_out, O3, not_16_out);
  and and_6 (and_6_out, not_17_out, not_18_out, not_19_out, not_20_out, not_21_out);
  and and_7 (and_7_out, not_22_out, not_23_out, O3, O2, not_24_out);
  and and_8 (and_8_out, not_25_out, not_26_out, not_27_out, not_28_out, O1, not_29_out);
  and and_9 (and_9_out, not_30_out, not_31_out, not_32_out, O2, not_33_out, not_34_out);
  and and_10 (and_10_out, not_35_out, not_36_out, not_37_out, not_38_out, O1, O0);
  and and_11 (and_11_out, not_39_out, not_40_out, not_41_out, O2, not_42_out, O0);
  and and_12 (and_12_out, not_43_out, not_44_out, O3, O2, O0);
  and and_13 (and_13_out, not_45_out, O4, not_46_out, not_47_out, not_48_out);
  and and_14 (and_14_out, not_49_out, O4, not_50_out, not_51_out, not_52_out);
  and and_15 (and_15_out, O3, not_53_out, O1, O0);
  and and_16 (and_16_out, O3, O2, not_54_out);
  and and_17 (and_17_out, O4, O1, O0);
  and and_18 (and_18_out, O4, O2);
  and and_19 (and_19_out, O4, O3);
  and and_20 (and_20_out, O3, not_55_out, not_56_out);
  and and_21 (and_21_out, O4, O1, O0);
  and and_22 (and_22_out, O4, O2);
  and and_23 (and_23_out, O4, O3);
  and and_24 (and_24_out, not_57_out, O2, O1, O0);
  and and_25 (and_25_out, O3, not_58_out, not_59_out, O0);
  and and_26 (and_26_out, O4, O1, O0);
  and and_27 (and_27_out, O4, O2);
  and and_28 (and_28_out, O4, O3);
  and and_29 (and_29_out, not_60_out, not_61_out, not_62_out, not_63_out, not_64_out, not_65_out);
  and and_30 (and_30_out, not_66_out, not_67_out, not_68_out, O1, O0);
  and and_31 (and_31_out, not_69_out, not_70_out, O3, O1);
  and and_32 (and_32_out, not_71_out, not_72_out, O3, O2, not_73_out);
  and and_33 (and_33_out, not_74_out, O4, not_75_out, not_76_out, O1, not_77_out);
  and and_34 (and_34_out, not_78_out, not_79_out, not_80_out, not_81_out, not_82_out);
  and and_35 (and_35_out, not_83_out, not_84_out, not_85_out, not_86_out, not_87_out);
  and and_36 (and_36_out, not_88_out, not_89_out, not_90_out, not_91_out, not_92_out);
  and and_37 (and_37_out, not_93_out, not_94_out, O3, O2, not_95_out);
  and and_38 (B0, not_96_out, not_97_out, O3, O1);
  and and_39 (and_39_out, not_98_out, not_99_out, not_100_out, not_101_out, O0);
  and and_40 (and_40_out, not_102_out, not_103_out, not_104_out, O1, not_105_out);
  and and_41 (and_41_out, not_106_out, not_107_out, not_108_out, O2, not_109_out);
  and and_42 (and_42_out, not_110_out, not_111_out, O3, O2, O0);
  and and_43 (and_43_out, not_112_out, O4, not_113_out, not_114_out, not_115_out);
  or or_1 (WriteA, and_1_out, and_2_out, and_3_out, and_4_out, and_5_out);
  or or_2 (WriteB, and_6_out, and_7_out);
  or or_3 (MemRead, and_8_out, and_9_out);
  or or_4 (MemWrite, and_10_out, and_11_out);
  or or_5 (PC, and_12_out, and_13_out, and_14_out);
  or or_6 (ALU2, and_15_out, and_16_out, and_17_out, and_18_out, and_19_out, O5);
  or or_7 (ALU1, and_20_out, and_21_out, and_22_out, and_23_out, O5);
  or or_8 (ALU0, and_24_out, and_25_out, and_26_out, and_27_out, and_28_out, O5);
  or or_9 (A0, and_29_out, and_30_out, and_31_out, and_32_out, and_33_out);
  or or_10 (A1, and_34_out, and_35_out, and_36_out, and_37_out);
  or or_11 (OFF, and_39_out, and_40_out, and_41_out, and_42_out, and_43_out);
endmodule

module ALU (
  input  [31:0] A,
  input  [2:0] in_2,
  input  [31:0] B,
  output [31:0] \output 
);

  wire [31:0] A___B, B____A, B____A_t, B___A;

  Adder #(.width(32)) adder_1 (.a(A), .b(B), .out(A___B));  // open: cin, cout
  Subtractor #(.width(32)) subtractor_1 (.a(B), .b(A), .out(B___A));  // open: bin, bout
  Shifter #(.width(32)) shifter_1 (.in(B), .\dist (A[4:0]), .out(B____A));
  Shifter #(.width(32), .shift("lr")) shifter_2 (.in(B), .\dist (A[4:0]), .out(B____A_t));
  Multiplexer #(.select(3), .width(32), .enable("false")) multiplexer_1 (
    .in0(A___B), .in1(B___A), .in2(B____A), .in3(B____A_t), .in4(A), .in5(B), .out(\output ), .sel(in_2));  // open: in6, in7
endmodule

module control (
  input  [7:0] in_1,
  output [1:0] PCSel,
  output WriteSP,
  output WriteA,
  output WriteB,
  output MemRead,
  output MemWrite,
  output PC,
  output [2:0] ALU,
  output [1:0] ASel,
  output [1:0] BSel,
  output offfset,
  output ALU_A,
  output data,
  output WriteSP_2,
  output SP_sel
);

  wire comparator_1_eq, comparator_2_eq, comparator_3_eq, comparator_4_eq, comparator_6_eq, comparator_7_eq,
       comparator_8_eq;

  Comparator comparator_1 (.a(in_1), .b(8'h11), .eq(comparator_1_eq));  // open: gt, lt
  Comparator comparator_2 (.a(in_1), .b(8'hd), .eq(comparator_2_eq));  // open: gt, lt
  Comparator comparator_3 (.a(in_1), .b(8'h12), .eq(comparator_3_eq));  // open: gt, lt
  Comparator comparator_4 (.a(in_1), .b(8'he), .eq(comparator_4_eq));  // open: gt, lt
  Comparator comparator_5 (.a(in_1), .b(8'hc), .eq(WriteSP));  // open: gt, lt
  Comparator comparator_6 (.a(in_1), .b(8'h3), .eq(comparator_6_eq));  // open: gt, lt
  Comparator comparator_7 (.a(in_1), .b(8'h2), .eq(comparator_7_eq));  // open: gt, lt
  or or_1 (ALU_A, comparator_6_eq, comparator_7_eq, comparator_8_eq);
  Comparator comparator_8 (.a(in_1), .b(8'ha), .eq(comparator_8_eq));  // open: gt, lt
  or or_2 (WriteSP_2, comparator_8_eq, SP_sel);
  Comparator comparator_9 (.a(in_1), .b(8'hb), .eq(SP_sel));  // open: gt, lt
  Comparator comparator_10 (.a(in_1), .b(8'h5), .eq(data));  // open: gt, lt
  opcode opcode_1 (
    .O5(in_1[5]), .O4(in_1[4]), .O3(in_1[3]), .O2(in_1[2]), .O1(in_1[1]), .O0(in_1[0]), .WriteA(WriteA),
    .WriteB(WriteB), .MemRead(MemRead), .MemWrite(MemWrite), .PC(PC), .ALU2(ALU[2]), .ALU1(ALU[1]),
    .ALU0(ALU[0]), .A0(ASel[0]), .A1(ASel[1]), .B0(BSel[0]), .OFF(offfset));
  or or_3 (PCSel[0], comparator_1_eq, comparator_2_eq, comparator_3_eq);
  or or_4 (PCSel[1], comparator_3_eq, comparator_4_eq);

  assign BSel[1] = 1'b0;
endmodule

module \or  (
  input  [7:0] in_1,
  input  in_2,
  input  in_3,
  input  [1:0] in_4,
  input  in_5,
  output [1:0] out_6
);

  wire and_1_out, and_2_out, comparator_1_eq, comparator_2_eq, or_2_out;
  wire [0:0] or_1_out;

  Multiplexer #(.width(2), .enable("false")) multiplexer_1 (
    .in0(in_4), .in1({in_4[1], or_1_out[0]}), .out(out_6), .sel(in_5));
  Comparator comparator_1 (.a(in_1), .b(8'h10), .eq(comparator_1_eq));  // open: gt, lt
  Comparator comparator_2 (.a(in_1), .b(8'h11), .eq(comparator_2_eq));  // open: gt, lt
  and and_1 (and_1_out, comparator_1_eq, in_2);
  and and_2 (and_2_out, in_3, comparator_2_eq);
  or or_1 (or_1_out[0], or_2_out, in_4[0]);
  or or_2 (or_2_out, and_1_out, and_2_out);
endmodule

module count (
  input  in_1,
  input  in_2,
  input  in_3,
  output out_4
);

  wire and_1_out;

  and and_1 (and_1_out, in_2, in_3);
  Multiplexer #(.enable("false")) multiplexer_1 (.in0(in_1), .out(out_4), .sel(and_1_out));  // open: in1
endmodule

module bcd (
  input  in_1,
  input  in_2,
  output [3:0] out_3,
  output [3:0] out_4,
  output [3:0] out_5,
  output [3:0] out_6,
  output [3:0] out_7
);

  wire comparator_1_eq, comparator_2_eq, comparator_3_eq, comparator_4_eq, comparator_5_eq, or_1_out,
       or_2_out, or_3_out, or_4_out, or_5_out;

  Counter #(.width(4), .max('hf)) counter_1 (
    .Q(out_3), .clk(comparator_2_eq), .clr(or_1_out));  // open: load, D, count, carry
  Comparator #(.width(4)) comparator_1 (.a(out_3), .b(4'b1010), .eq(comparator_1_eq));  // open: gt, lt
  or or_1 (or_1_out, comparator_1_eq, in_2);
  Counter #(.width(4), .max('hf)) counter_2 (
    .Q(out_4), .clk(comparator_3_eq), .clr(or_2_out));  // open: load, D, count, carry
  or or_2 (or_2_out, comparator_2_eq, in_2);
  Counter #(.width(4), .max('hf)) counter_3 (
    .Q(out_5), .clk(comparator_4_eq), .clr(or_3_out));  // open: load, D, count, carry
  Comparator #(.width(4)) comparator_2 (.a(out_4), .b(4'b1010), .eq(comparator_2_eq));  // open: gt, lt
  Comparator #(.width(4)) comparator_3 (.a(out_5), .b(4'b1010), .eq(comparator_3_eq));  // open: gt, lt
  or or_3 (or_3_out, comparator_3_eq, in_2);
  Counter #(.width(4), .max('hf)) counter_4 (
    .Q(out_6), .clk(comparator_5_eq), .clr(or_4_out));  // open: load, D, count, carry
  or or_4 (or_4_out, comparator_4_eq, in_2);
  Counter #(.width(4), .max('hf)) counter_5 (.Q(out_7), .clk(in_1), .clr(or_5_out));  // open: load, D, count, carry
  Comparator #(.width(4)) comparator_4 (.a(out_6), .b(4'b1010), .eq(comparator_4_eq));  // open: gt, lt
  Comparator #(.width(4)) comparator_5 (.a(out_7), .b(4'b1010), .eq(comparator_5_eq));  // open: gt, lt
  or or_5 (or_5_out, comparator_5_eq, in_2);
endmodule

module \new  (
  input  in_1,
  input  in_2,
  input  [1:0] in_3,
  input  in_4,
  output [1:0] out_5
);

  wire or_2_out;
  wire [0:0] or_1_out;

  Multiplexer #(.width(2), .enable("false")) multiplexer_1 (
    .in0(in_3), .in1({in_3[1], or_1_out[0]}), .out(out_5), .sel(in_4));
  or or_1 (or_1_out[0], or_2_out, in_3[0]);
  or or_2 (or_2_out, in_1, in_2);
endmodule
